# Fritzing sketch skemaRangkaian (saved by Fritzing 0.9.3b)

parts:
  M1 = DOIT Esp32 DevKit v1 (30 pins long, 11 pins width) [part_number=ESP32S-PIN30]
  Part1 = LCD1602-I2C
  A1 = 2957N11 pressure sensor
  J1 = Piezo Speaker

nets:
  N1: M1.3V3, J1.pin2
  N2: M1.D15, J1.pin1
  N3: M1.D21, Part1.SDA
  N4: M1.D22, Part1.SCL
  N5: M1.D35, A1.Pin_3
  GND: M1.GND, Part1.GND, A1.Pin_1
  VIN: M1.VIN, Part1.VCC, A1.Pin_2

custom parts:
  DOIT Esp32 DevKit v1 (30 pins long, 11 pins width): The DOIT Esp32 DevKit v1 is one of the development board created by DOIT to evaluate the ESP-WROOM-32 module. It is based on the ESP32 microcontroller that boasts Wifi, Bluetooth, Ethernet and Low Power support all in a single chip. (vanepp) made breadboard work, adjusted pin numbering and labels and reduced size of schematic and cleaned up pcb. This chip is 30pins long (2 x15) and 11 pins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
  LCD1602-I2C: A standard character display, usually with 2x16 characters. Comes in many colors with LCM1602 IIC attached.
  2957N11 pressure sensor: Monitor and control vacuum pumps, air compressors, and hydraulics. These transmitters convert both pressure and vacuum into an electrical signal that can be interpreted by receiving devices, such as remote displays, programmable logic controllers, and motor speed controls.
